# Fritzing sketch controller (saved by Fritzing 0.9.1b)
perfboards: 1

parts:
  Pro_Micro1 = Pro Micro
  12V_Plug = Power plug
  R4 = Resistor [tolerance=±5% resistance=10k package=THT]
  R1 = Resistor [tolerance=±5% resistance=14k package=THT]
  R5 = Resistor [tolerance=±5% resistance=14k package=THT]
  R6 = Resistor [tolerance=±5% resistance=220 package=THT]
  R7 = Resistor [tolerance=±5% resistance=220 package=THT]
  MJE3055 = npn-Powertransistor [package="TO220 [THT]"]
  R3 = Resistor [tolerance=±5% resistance=10k package=THT]
  LCD1 = LCD screen
  MJE3055_2 = npn-Powertransistor [package="TO220 [THT]"]
  B_Strike = Solenoid
  A_Strike = Solenoid
  Data_0 = Pushbutton [package=THT]
  Data_1 = Pushbutton [package=THT]
  Data_0_2 = Pushbutton [package=THT]
  Data_1_2 = Pushbutton [package=THT]
  A_Success = LED - 3mm [color="Green (570nm)" package="3 mm [THT]"]
  B_Success = LED - 3mm [color="Green (570nm)" package="3 mm [THT]"]

nets:
  N1: Pro_Micro1.TX1, R4.Pin_1, R1.Pin_0
  N2: Pro_Micro1.RX0, R5.Pin_0, R3.Pin_1
  N3: Pro_Micro1.D2, Data_0_2.leg0
  N4: Pro_Micro1.D3, Data_1_2.leg0
  N5: Pro_Micro1.D5, R7.Pin_0
  N6: Pro_Micro1.D6, R6.Pin_0
  N7: Pro_Micro1.D8, A_Success.cathode
  N8: Pro_Micro1.D9, B_Success.cathode
  N9: Pro_Micro1.D10, LCD1.RS
  N10: Pro_Micro1.D16/MOSI, LCD1.R/W
  N11: Pro_Micro1.D14/MISO, LCD1.E
  N12: Pro_Micro1.D15/SCLK, LCD1.DB4
  N13: Pro_Micro1.D18/A0, LCD1.DB5
  N14: Pro_Micro1.D19/A1, LCD1.DB6
  N15: Pro_Micro1.D20/A2, LCD1.DB7
  VCC: Pro_Micro1.VCC, LCD1.VDD
  GND: Pro_Micro1.GND, 12V_Plug.GND, R4.Pin_0, MJE3055.emitter, R3.Pin_0, MJE3055_2.emitter
  N16: Pro_Micro1.RAW, 12V_Plug.VCC, B_Strike.pin1, A_Strike.pin1, Data_0.leg1, Data_1.leg1, Data_0_2.leg1, Data_1_2.leg1, A_Success.anode, B_Success.anode
  N17: R1.Pin_1, Data_1.leg0
  N18: R5.Pin_1, Data_0.leg0
  N19: R6.Pin_1, MJE3055.base
  N20: R7.Pin_1, MJE3055_2.base
  N21: MJE3055.collector, B_Strike.pin2
  N22: LCD1.VSS, LCD1.V0
  N23: MJE3055_2.collector, A_Strike.pin2

notes:
  HID Reader
  UTC Reader

custom parts:
  Pro Micro: The SparkFun Pro Micro is a complete USB-based microcontoller development system, in a very small footprint, capable of implementing many types of projects. All programming can be done via the USB port.
